// Logisim project CS115B.circ as structural Verilog: 5 circuits, main circuit myXOR
// XOR
module myXOR (
  input  X,
  input  Y,
  output \output 
);

  wire and_1_out, and_2_out, not_1_out, not_2_out;

  not not_1 (not_1_out, X);
  not not_2 (not_2_out, Y);
  and and_1 (and_1_out, not_1_out, Y);
  and and_2 (and_2_out, X, not_2_out);
  or or_1 (\output , and_1_out, and_2_out);
endmodule

module HalfAdder (
  input  X,
  input  Y,
  output out_3,
  output out_4
);

  myXOR myxor_1 (.X(X), .Y(Y), .\output (out_3));
  and and_1 (out_4, X, Y);

  // Notes on the sheet:
  //   Shows when 2 outputs are true only when both inuts are 1 
endmodule

module fullAdder (
  input  A,
  input  B,
  input  C,
  output S,
  output C_2
);

  wire and_1_out, and_2_out, myxor_1_output;

  myXOR myxor_1 (.X(A), .Y(B), .\output (myxor_1_output));
  and and_1 (and_1_out, A, B);
  myXOR myxor_2 (.X(myxor_1_output), .Y(C), .\output (S));
  and and_2 (and_2_out, myxor_1_output, C);
  or or_1 (C_2, and_2_out, and_1_out);

  // Notes on the sheet:
  //   (+) exclusive or
  //   A or B
  //   A(+)B
  //   AB
  //   A B C
  //   (A(+)B)C +AB
  //   0
  //   000
  //   001
  //   010
  //   look at paper
  //   011
  //   100
  //   101
  //   110
  //   111
  //   (A(+)B)C
  //   C
  //   A(+)B(+)C
  //   (A(+)B)C + AB
  //   S
  //   A(+)B(+)C
endmodule

module S_R_Latch (
  input  S,
  input  R,
  output not_Q,
  output Q
);

  nor nor_1 (not_Q, S, Q);
  nor nor_2 (Q, not_Q, R);
endmodule

module D_Latch (
  input  D,
  input  Strobe,
  output Not_Q,
  output Q
);

  wire and_1_out, and_2_out, not_1_out;

  not not_1 (not_1_out, D);
  and and_1 (and_1_out, D, Strobe);
  and and_2 (and_2_out, not_1_out, Strobe);
  S_R_Latch s_r_latch_1 (.S(and_1_out), .R(and_2_out), .not_Q(Not_Q), .Q(Q));

  // Notes on the sheet:
  //   when enabled
  //   Dlatch
  //   1-bit memory circuit stores, or latches on, to a "high" or "low"
  //   state when disabled, and reads new data from the D input
endmodule
